# Fritzing sketch car_diagram (saved by Fritzing 0.9.3b)

parts:
  Arduino_UNO = Arduino Uno (Rev3)
  Raspberry_Pi = Raspberry Pi 3 [part_number=RPI-3-V1.2]
  M1 = DC Motor  # not connected
  M2 = DC Motor
  M3 = DC Motor
  M4 = DC Motor  # not connected
  l298n = L298_BRIDGE_DRIVER [package=powerso20]
  l298n_2 = L298_BRIDGE_DRIVER [package=powerso20]
  CAMERA = TTL Serial JPEG Camera  # not connected
  hc-sr1 = hc-sr04
  hc-sr2 = hc-sr04
  J1 = Basic Servo
  J2 = Basic Servo
  BAT1 = Battery Holders [package=lipo-1100mAh]  # not connected

nets:
  N1: Arduino_UNO.A0, hc-sr1.Trig
  N2: Arduino_UNO.A1, hc-sr1.Echo
  N3: Arduino_UNO.A2, hc-sr2.Trig
  N4: Arduino_UNO.A3, hc-sr2.Echo
  N5: Arduino_UNO.A4/SDA, Raspberry_Pi.GPIO2
  N6: Arduino_UNO.A5/SCL, Raspberry_Pi.GPIO3
  N7: Arduino_UNO.D8, l298n_2.IN3
  GND: Arduino_UNO.D10_PWM/SS, Arduino_UNO.GND, Raspberry_Pi.GND, M2.pin_1, M3.pin_2, l298n.GND, l298n_2.GND, hc-sr1.GND, hc-sr2.GND, J1.gnd, J2.gnd
  N8: Arduino_UNO.D11_PWM/MOSI, l298n_2.IN4
  N9: Arduino_UNO.D12/MISO, l298n_2.OUT3
  N10: Arduino_UNO.D1/TX, l298n.IN1
  N11: Arduino_UNO.D2, l298n.VS
  N12: Arduino_UNO.D3_PWM, l298n.OUT2
  N13: Arduino_UNO.D4, l298n.OUT1
  N14: Arduino_UNO.D5_PWM, J1.pulse
  N15: Arduino_UNO.D6_PWM, J2.pulse
  N16: Arduino_UNO.D7, l298n_2.ENB
  VCC: Arduino_UNO.5V, hc-sr1.VCC, hc-sr2.VCC, J1.vcc, J2.vcc
  N17: M2.pin_2, l298n_2.SENSE_B
  N18: M3.pin_1, l298n_2.SENSE_A

custom parts:
  TTL Serial JPEG Camera: TTL Serial JPEG Camera with NTSC Out
